# Fritzing sketch scare-pi (saved by Fritzing 1.0.8)
breadboards: 1

parts:
  MAX98357A_Vin_GND_BCLK_LRC_DIN_SD_GAIN = female pin header, 7 pins [form="♀ (female rounded)"]
  Right_eye_0x71_(A0_bridged) = 1.2 Inch 8x8 LED Matrix Backpack [part_number=1632]
  Left_eye_0x70 = 1.2 Inch 8x8 LED Matrix Backpack [part_number=1632]
  Raspberry_Pi_Zero_2_W = Raspberry Pi Zero
  LD2420_radar_VCC_GND_OT1_RX = female pin header, 4 pins [form="♀ (female)"]

nets:
  N1: MAX98357A_Vin_GND_BCLK_LRC_DIN_SD_GAIN.pin1, Raspberry_Pi_Zero_2_W.pin_35
  N2: MAX98357A_Vin_GND_BCLK_LRC_DIN_SD_GAIN.pin2, Raspberry_Pi_Zero_2_W.pin_18
  N3: MAX98357A_Vin_GND_BCLK_LRC_DIN_SD_GAIN.pin3, Raspberry_Pi_Zero_2_W.pin_40
  GND: MAX98357A_Vin_GND_BCLK_LRC_DIN_SD_GAIN.pin4, MAX98357A_Vin_GND_BCLK_LRC_DIN_SD_GAIN.pin6, Right_eye_0x71_(A0_bridged).GND, Left_eye_0x70.GND, Raspberry_Pi_Zero_2_W.pin_1, Raspberry_Pi_Zero_2_W.pin_6, Raspberry_Pi_Zero_2_W.pin_17, Raspberry_Pi_Zero_2_W.pin_20, Raspberry_Pi_Zero_2_W.pin_25, Raspberry_Pi_Zero_2_W.pin_34, Raspberry_Pi_Zero_2_W.pin_39, LD2420_radar_VCC_GND_OT1_RX.pin2
  N4: MAX98357A_Vin_GND_BCLK_LRC_DIN_SD_GAIN.pin5, Raspberry_Pi_Zero_2_W.pin_7
  N5: MAX98357A_Vin_GND_BCLK_LRC_DIN_SD_GAIN.pin7, Raspberry_Pi_Zero_2_W.pin_2, Raspberry_Pi_Zero_2_W.pin_4
  N6: Right_eye_0x71_(A0_bridged).SCL, Left_eye_0x70.SCL, Raspberry_Pi_Zero_2_W.pin_5
  N7: Right_eye_0x71_(A0_bridged).SDA, Left_eye_0x70.SDA, Raspberry_Pi_Zero_2_W.pin_3
  VDD: Right_eye_0x71_(A0_bridged).VDD, Left_eye_0x70.VDD, LD2420_radar_VCC_GND_OT1_RX.pin1
  N8: Raspberry_Pi_Zero_2_W.pin_8, LD2420_radar_VCC_GND_OT1_RX.pin3
  N9: Raspberry_Pi_Zero_2_W.pin_10, LD2420_radar_VCC_GND_OT1_RX.pin4

notes:
  MAX98357, LRCLK, BCLK, DIN, GAIN, GND, VIN (5V)
  LD2420, 3V3, GND, OT1, RX
